# Fritzing sketch GamingTable Final (saved by Fritzing 0.9.3b)
circuit board: 5.64444cm x 8.46667cm
breadboards: 1

parts:
  10k = Resistor [tolerance=±5% resistance=10k package=THT]
  10k_2 = Resistor [tolerance=±5% resistance=10k package=THT]
  470 = Resistor [tolerance=±5% resistance=470 package=THT]
  470_2 = Resistor [tolerance=±5% resistance=470 package=THT]
  ADS1015 = female pin header, 10 pins [form="♀ (female)"]
  J2 = Generic double row male header - 40 pins [form="♂ (male)" package=THT]
  Y = female pin header, 2 pins [form="♀ (female)"]
  A = female pin header, 2 pins [form="♀ (female)"]
  B = female pin header, 2 pins [form="♀ (female)"]
  Start = female pin header, 2 pins [form="♀ (female)"]
  10k_3 = Resistor [tolerance=±5% resistance=10k package=THT]
  10k_4 = Resistor [tolerance=±20% resistance=10k package=THT]
  10k_5 = Resistor [tolerance=±5% resistance=10k package=THT]
  10k_6 = Resistor [tolerance=±5% resistance=10k package=THT]
  10k_7 = Resistor [tolerance=±5% resistance=10k package=THT]
  10k_8 = Resistor [tolerance=±5% resistance=10k package=THT]
  10k_9 = Resistor [tolerance=±5% resistance=10k package=THT]
  JoyRight1 = female pin header, 5 pins [form="♀ (female)"]
  JoyLeft = female pin header, 5 pins [form="♀ (female)"]
  X = female pin header, 2 pins [form="♀ (female)"]
  Select = female pin header, 2 pins [form="♀ (female)"]
  Right = female pin header, 2 pins [form="♀ (female)"]
  Up = female pin header, 2 pins [form="♀ (female)"]
  Down = female pin header, 2 pins [form="♀ (female)"]
  Left1 = female pin header, 2 pins [form="♀ (female)"]
  10k_10 = Resistor [tolerance=±5% resistance=10k package=THT]
  10k_11 = Resistor [tolerance=±5% resistance=10k package=THT]
  10k_12 = Resistor [tolerance=±5% resistance=10k package=THT]
  10k_13 = Resistor [tolerance=±5% resistance=10k package=THT]
  10k_14 = Resistor [tolerance=±5% resistance=10k package=THT]
  10k_15 = Resistor [tolerance=±5% resistance=10k package=THT]
  Bumpers = female pin header, 4 pins [form="♀ (female)"]
  10k_16 = Resistor [tolerance=±5% resistance=10k package=THT]

nets:
  N1: 10k.Pin_0, ADS1015.pin3, J2.GPIO3_(SCL1)
  N2: 10k.Pin_1, 10k_2.Pin_1, 470_2.Pin_1, ADS1015.pin1, J2.5V, 10k_15.Pin_1, 10k_16.Pin_1
  N3: 10k_2.Pin_0, ADS1015.pin4, J2.GPIO2_(SDA1)
  N4: 470.Pin_0, J2.3V3
  N5: 470.Pin_1, Right.pin2, Up.pin2, Down.pin2, Left1.pin2, Bumpers.pin2, Bumpers.pin4
  N6: 470_2.Pin_0, JoyRight1.pin2, JoyLeft.pin2
  N7: ADS1015.pin2, J2.GND, 10k_3.Pin_0, 10k_4.Pin_0, 10k_5.Pin_0, 10k_6.Pin_0, 10k_7.Pin_0, 10k_8.Pin_0, 10k_9.Pin_1, JoyRight1.pin1, JoyLeft.pin1, 10k_10.Pin_1, 10k_11.Pin_1, 10k_12.Pin_1, 10k_13.Pin_1, 10k_14.Pin_1
  N8: ADS1015.pin7, JoyRight1.pin3
  N9: ADS1015.pin8, JoyRight1.pin4
  N10: ADS1015.pin9, JoyLeft.pin3
  N11: ADS1015.pin10, JoyLeft.pin4
  N12: J2.GPIO17, JoyLeft.pin5, 10k_16.Pin_0
  N13: J2.GPIO27, JoyRight1.pin5, 10k_15.Pin_0
  N14: J2.GPIO19, 10k_13.Pin_0, Bumpers.pin1
  N15: J2.GPIO26, 10k_12.Pin_0, Bumpers.pin3
  N16: J2.GPIO21, Up.pin1, 10k_11.Pin_0
  N17: J2.GPIO20, 10k_9.Pin_0, Down.pin1
  N18: J2.GPIO16, Left1.pin1, 10k_10.Pin_0
  N19: J2.GPIO12, Right.pin1, 10k_14.Pin_0
  N20: J2.GPIO07, Start.pin1, 10k_8.Pin_1
  N21: J2.GPIO08, 10k_7.Pin_1, Select.pin1
  N22: J2.GPIO25, B.pin1, 10k_6.Pin_1
  N23: J2.GPIO24, Y.pin1, 10k_4.Pin_1
  N24: J2.GPIO23, 10k_3.Pin_1, X.pin1
  N25: J2.GPIO18, A.pin1, 10k_5.Pin_1
  N26: Y.pin2, A.pin2, B.pin2, Start.pin2, X.pin2, Select.pin2

custom parts:
  Generic double row male header - 40 pins: Generic double row male header
